// Logisim project organizacion.circ as structural Verilog: 6 circuits, main circuit main
module main (
);

  // NOT_Gate not_1 is placed but not wired
endmodule

module Not16 (
  input  [15:0] in_1,
  output [15:0] out_2
);

  not not_1 (out_2[0], in_1[0]);
  not not_2 (out_2[1], in_1[1]);
  not not_3 (out_2[2], in_1[2]);
  not not_4 (out_2[3], in_1[3]);
  not not_5 (out_2[4], in_1[4]);
  not not_6 (out_2[5], in_1[5]);
  not not_7 (out_2[6], in_1[6]);
  not not_8 (out_2[7], in_1[7]);
  not not_9 (out_2[8], in_1[8]);
  not not_10 (out_2[9], in_1[9]);
  not not_11 (out_2[10], in_1[10]);
  not not_12 (out_2[11], in_1[11]);
  not not_13 (out_2[12], in_1[12]);
  not not_14 (out_2[13], in_1[13]);
  not not_15 (out_2[14], in_1[14]);
  not not_16 (out_2[15], in_1[15]);
endmodule

module AND16 (
  input  [15:0] a,
  input  [15:0] b
);

  wire undriven;

  // AND_Gate and_1 has open pins: in0=a[0], in1=b[0], out=open
  // AND_Gate and_2 has open pins: in0=a[1], in1=b[1], out=open
  // AND_Gate and_3 has open pins: in0=a[2], in1=b[2], out=open
  // AND_Gate and_4 has open pins: in0=a[3], in1=b[3], out=open
  // AND_Gate and_5 has open pins: in0=a[4], in1=b[4], out=open
  // AND_Gate and_6 has open pins: in0=a[5], in1=b[5], out=open
  // AND_Gate and_7 has open pins: in0=a[6], in1=b[6], out=open
  // AND_Gate and_8 has open pins: in0=a[8], in1=b[8], out=open
  // AND_Gate and_9 has open pins: in0=undriven, in1=b[12], out=open
  // AND_Gate and_10 has open pins: in1=b[13], out=open
  // AND_Gate and_11 has open pins: in1=b[14], out=open
  // AND_Gate and_12 has open pins: in1=b[15], out=open
  // AND_Gate and_13 has open pins: in0=a[7], in1=b[7], out=open
  // AND_Gate and_14 has open pins: in0=a[9], in1=b[9], out=open
  // AND_Gate and_15 has open pins: in0=a[10], in1=b[10], out=open
  // AND_Gate and_16 has open pins: in0=a[11], in1=b[11], out=open
endmodule

module mux (
  input  sel,
  input  a,
  input  sel2,
  input  b,
  output out_5
);

  wire and_1_out, and_2_out, not_1_out;

  not not_1 (not_1_out, sel);
  and and_1 (and_1_out, not_1_out, a);
  and and_2 (and_2_out, sel2, b);
  or or_1 (out_5, and_1_out, and_2_out);
endmodule

module Bit (
  input  in_1,
  input  in_2,
  output out_3
);

  wire clock_1_out, multiplexer_1_out, undriven;

  Clock clock_1 (.out(clock_1_out));
  Multiplexer multiplexer_1 (.in0(out_3), .in1(in_1), .out(multiplexer_1_out), .sel(in_2));  // open: en
  D_Flip_Flop d_ff_1 (
    .clk(clock_1_out), .D(multiplexer_1_out), .Q(out_3), .preset(undriven), .en(undriven));  // open: Qn, reset
endmodule

module registro (
  input  [15:0] in,
  input  in_2
);

  wire undriven;

  Bit bit_1 (.in_1(in_2), .in_2(in[0]));  // open: out_3
  Bit bit_2 (.in_2(in[2]));  // open: in_1, out_3
  Bit bit_3 (.in_2(in[4]));  // open: in_1, out_3
  Bit bit_4 (.in_2(in[6]));  // open: in_1, out_3
  Bit bit_5 (.in_2(in[8]));  // open: in_1, out_3
  Bit bit_6 (.in_2(in[10]));  // open: in_1, out_3
  Bit bit_7 (.in_2(in[12]));  // open: in_1, out_3
  Bit bit_8 (.in_2(in[14]));  // open: in_1, out_3
  Bit bit_9 (.in_1(undriven), .in_2(in[1]));  // open: out_3
  Bit bit_10 (.in_2(in[3]));  // open: in_1, out_3
  Bit bit_11 (.in_2(in[5]));  // open: in_1, out_3
  Bit bit_12 (.in_2(in[7]));  // open: in_1, out_3
  Bit bit_13 (.in_1(in[9]));  // open: in_2, out_3
  Bit bit_14 (.in_2(in[11]));  // open: in_1, out_3
  Bit bit_15 (.in_2(in[13]));  // open: in_1, out_3
  Bit bit_16 (.in_2(in[15]));  // open: in_1, out_3
endmodule
